# Fritzing sketch main (saved by Fritzing 1.0.6)
breadboards: 1

parts:
  M1 = STM32F103C8T6 blue mini board
  R1 = Resistor [tolerance=±5% power=0.25W resistance=1k package=THT]
  LED1 = LED - 5mm [color="Red (633nm)" current=0.030A package="5 mm [THT]"]

nets:
  N1: M1.B13, LED1.anode
  N2: M1.G, M1.GND, R1.Pin_0
  N3: R1.Pin_1, LED1.cathode
