# Fritzing sketch main (saved by Fritzing 1.0.6)
breadboards: 1

parts:
  M1 = STM32F103C8T6 blue mini board
  R1 = Resistor [tolerance=±5% power=0.25W resistance=1k package=THT]
  LED1 = LED - 5mm [color="Red (633nm)" current=0.030A package="5 mm [THT]"]
  VCC1 = Battery [internal_resistance=0.1Ω]

nets:
  N1: M1.B12, LED1.anode
  N2: M1.G, M1.GND, R1.Pin_0, VCC1.-
  N3: M1.3.3V, VCC1.+
  N4: R1.Pin_1, LED1.cathode
